# Fritzing sketch proto (saved by Fritzing 0.9.4)
circuit board: 8.46667cm x 5.64444cm
breadboards: 1

parts:
  U1 = ESP8266 NodeMCU LoLin module
  R2 = Resistor [tolerance=±5% resistance=220 package=THT]
  R3 = Resistor [tolerance=±5% resistance=220 package=THT]
  R4 = Resistor [tolerance=±5% resistance=220 package=THT]
  RHT1 = Humidity and Temperature Sensor RHT03
  LED9 = smd LED [color="Infrared (940nm)" package="0805 [SMD]"]
  LED11 = smd LED [color="Infrared (940nm)" package="0805 [SMD]"]
  LED12 = smd LED [color="Infrared (940nm)" package="0805 [SMD]"]
  KY-1 = Keyes Relay [package=THT]
  Lampada = LEDs [package=led10mm]

nets:
  N1: U1.D1, RHT1.Data-signal
  N2: U1.D2, KY-1.signal
  N3: U1.D4, LED9.anode
  3V3: U1.3V3, RHT1.Vcc, KY-1.power
  N4: U1.GND, R2.Pin_1, R3.Pin_1, R4.Pin_1, RHT1.GND_2, KY-1.ground
  N5: U1.D5, LED11.anode
  N6: U1.D7, LED12.anode
  N7: R2.Pin_0, LED9.cathode
  N8: R3.Pin_0, LED11.cathode
  N9: R4.Pin_0, LED12.cathode
  N10: KY-1.NC, KY-1.C, KY-1.NO, Lampada.C

notes:
  Cabo de Força Rabicho

custom parts:
  ESP8266 NodeMCU LoLin module: ESP8266 based NodeMCU
  Keyes Relay: The Keyes 5V relay module is suitable for SCM development, home appliance control. It uses a 5V~12V TIL control signal which can control DC / AC signal.
  LEDs: LEDs Standard schematic elements and footprints for 5mm, 3mm, 1206, and 0603 sized LEDs. 5mm - Spark Fun Electronics SKU : COM-00529 (and others)
